// Logisim project encoder42.circ as structural Verilog: 1 circuit, main circuit main
module main (
  input  A0,
  input  A1,
  input  A2,
  input  A3,
  output Y0,
  output Y1
);

  or or_1 (Y0, A1, A3);
  or or_2 (Y1, A2, A3);
endmodule
